# Fritzing sketch ESP-to-Attiny-Joystick-client (saved by Fritzing 0.9.2b)

parts:
  U2 = attiny85 [package=dip]
  POT1 = Analog Thumb Joystick
  LED1 = LED - 5mm [color="Red (633nm)" package="5 mm [THT]"]
  LED2 = LED - 5mm [color="Green (570nm)" package="5 mm [THT]"]
  LED3 = LED - 5mm [color="Red (633nm)" package="5 mm [THT]"]
  LED4 = LED - 5mm [color="Green (570nm)" package="5 mm [THT]"]
  LED5 = LED - 5mm [color="Blue (525nm)" package="5 mm [THT]"]
  R1 = Resistor [tolerance=±5% resistance=220 package=THT]
  R2 = Resistor [tolerance=±5% resistance=220 package=THT]
  R3 = Resistor [tolerance=±5% resistance=220 package=THT]
  R4 = Resistor [tolerance=±5% resistance=220 package=THT]
  R5 = Resistor [tolerance=±5% resistance=220 package=THT]
  U4 = ESP8266 WiFi Module [part_number=ESP8266]
  R6 = Resistor [tolerance=±5% resistance=10k package=THT]

nets:
  N1: U2.Pin_1, R6.Pin_1
  X Axis: U2.Pin_2, POT1.Xout
  Y Axis: U2.Pin_3, POT1.Yout
  GND: U2.Pin_4, POT1.GND, LED1.cathode, LED2.cathode, LED3.cathode, LED4.cathode, LED5.cathode, U4.GND
  N2: U2.Pin_5, U4.TXD
  N3: U2.Pin_6, U4.RXD
  button: U2.Pin_7, POT1.Select
  3.3V: U2.Pin_8, POT1.Vcc, U4.VCC, R6.Pin_0
  N4: LED1.anode, R1.Pin_1
  N5: LED2.anode, R2.Pin_1
  N6: LED3.anode, R3.Pin_1
  N7: LED4.anode, R4.Pin_1
  N8: LED5.anode, R5.Pin_0
  N9: R1.Pin_0, U4.GPIO_13
  N10: R2.Pin_0, U4.GPIO_12
  N11: R3.Pin_0, U4.GPIO_14
  N12: R4.Pin_0, U4.GPIO_16
  N13: R5.Pin_1, U4.GPIO_15

custom parts:
  ESP8266 WiFi Module: Generic WiFi Module based on the ESP8266 with onboard PCB antenna and UART communications
